# Fritzing sketch cwrm (saved by Fritzing 0.9.3b)
circuit board: 3cm x 1.6cm
breadboards: 1

parts:
  U1 = ESP8266 WiFi Module [part_number=ESP8266]
  Q1 = NPN-Transistor [part_number=2N2222 package="TO92 [THT]"]
  R1 = Resistor [tolerance=±5% resistance=2.2k package=THT]
  R2 = Resistor [tolerance=±5% resistance=2.2k package=THT]
  J1 = female pin header, 3 pins [form="♀ (female)"]
  Q2 = NPN-Transistor [part_number=2N2222 package="TO92 [THT]"]

nets:
  N1: U1.VCC, U1.CH_PD
  N2: U1.GPIO_0, R2.Pin_0
  N3: U1.GPIO_2, R1.Pin_0
  GND: U1.GND, Q1.E, J1.pin2, Q2.E
  N4: Q1.B, R1.Pin_1
  N5: Q1.C, J1.pin1
  N6: R2.Pin_1, Q2.B
  N7: J1.pin3, Q2.C

notes:
  CWRM v1.0
  s
  f
  - Shutter
  - GND
  - Focus
  willdurand

custom parts:
  ESP8266 WiFi Module: Generic WiFi Module based on the ESP8266 with onboard PCB antenna and UART communications
